// Logisim project Logisim_project_Sania_25125033.circ as structural Verilog: 9 circuits, main circuit imm_gen
module imm_gen (
  input  [31:0] ins,
  output [31:0] imm
);

  wire B_op, comparator_1_eq, comparator_2_eq, comparator_3_eq, comparator_6_eq, comparator_7_eq, I_op, J_op,
       S_op, U_op;
  wire [2:0] priority_encoder_1_out;
  wire [31:0] B_imm, I_imm, J_imm, S_imm;

  assign J_imm = {{11{ins[31]}}, {ins[31], ins[19:12], ins[20], ins[30:21], 1'b0}};  // Bit_Extender bit_extender_1
  assign S_imm = {{20{ins[31]}}, {ins[31:25], ins[11:7]}};  // Bit_Extender bit_extender_2
  assign I_imm = {{20{ins[31]}}, ins[31:20]};  // Bit_Extender bit_extender_3
  assign B_imm = {{19{ins[31]}}, {ins[31], ins[7], ins[30:25], ins[11:8], 1'b0}};  // Bit_Extender bit_extender_4
  Comparator #(.width(7)) comparator_1 (.a(ins[6:0]), .b(7'b0010011), .eq(comparator_1_eq));  // open: gt, lt
  Comparator #(.width(7)) comparator_2 (.a(ins[6:0]), .b(7'b0000011), .eq(comparator_2_eq));  // open: gt, lt
  Comparator #(.width(7)) comparator_3 (.a(ins[6:0]), .b(7'b1100111), .eq(comparator_3_eq));  // open: gt, lt
  Comparator #(.width(7)) comparator_4 (.a(ins[6:0]), .b(7'b0100011), .eq(S_op));  // open: gt, lt
  Comparator #(.width(7)) comparator_5 (.a(ins[6:0]), .b(7'b1100011), .eq(B_op));  // open: gt, lt
  Comparator #(.width(7)) comparator_6 (.a(ins[6:0]), .b(7'b0110111), .eq(comparator_6_eq));  // open: gt, lt
  Comparator #(.width(7)) comparator_7 (.a(ins[6:0]), .b(7'b0010111), .eq(comparator_7_eq));  // open: gt, lt
  Comparator #(.width(7)) comparator_8 (.a(ins[6:0]), .b(7'b1101111), .eq(J_op));  // open: gt, lt
  Multiplexer #(.disabled("Z"), .enable("true"), .select(3), .width(32)) multiplexer_1 (
    .in0(I_imm), .in1(S_imm), .in2(B_imm), .in3({ins[31:12], {12{1'b0}}}), .in4(J_imm), .in5({32{1'b0}}),
    .in6({32{1'b0}}), .in7({32{1'b0}}), .out(imm), .sel(priority_encoder_1_out));  // open: en
  or or_1 (I_op, comparator_1_eq, comparator_2_eq, comparator_3_eq);
  or or_2 (U_op, comparator_6_eq, comparator_7_eq);
  Priority_Encoder priority_encoder_1 (
    .in0(I_op), .in1(S_op), .in2(B_op), .in3(U_op), .in4(J_op), .out(priority_encoder_1_out));  // open: in5, in6, in7, en_in, gs, en_out

  // Other names for the same wires on the sheet: op[6:0] = ins[6:0]; U_imm[31:12] = ins[31:12]
endmodule

module Load_Handler (
  input  [31:0] mem_data,
  input  [2:0] fun3,
  output [31:0] Load_output
);

  wire [31:0] bit_extender_1_out, bit_extender_2_out, bit_extender_3_out, bit_extender_4_out;

  assign bit_extender_1_out = {{24{mem_data[7]}}, mem_data[7:0]};  // Bit_Extender bit_extender_1
  assign bit_extender_2_out = {{24{1'b0}}, mem_data[7:0]};  // Bit_Extender bit_extender_2
  assign bit_extender_3_out = {{16{mem_data[15]}}, mem_data[15:0]};  // Bit_Extender bit_extender_3
  assign bit_extender_4_out = {{16{1'b0}}, mem_data[15:0]};  // Bit_Extender bit_extender_4
  Multiplexer #(.disabled("Z"), .enable("true"), .select(3), .width(32)) multiplexer_1 (
    .in0(bit_extender_1_out), .in1(bit_extender_3_out), .in2(mem_data), .in3(mem_data),
    .in4(bit_extender_2_out), .in5(bit_extender_4_out), .in6(mem_data), .in7(mem_data), .out(Load_output),
    .sel(fun3));  // open: en
endmodule

module branchcomparator (
  input  [31:0] rdata1,
  input  branch,
  input  [31:0] rdata2,
  input  [2:0] fun3,
  output branch_taken
);

  wire comparator_1_eq, comparator_1_gt, comparator_1_lt, comparator_2_eq, comparator_2_gt, comparator_2_lt,
       multiplexer_1_out, not_1_out, or_1_out, or_2_out;

  Comparator #(.width(32)) comparator_1 (
    .a(rdata1), .b(rdata2), .gt(comparator_1_gt), .eq(comparator_1_eq), .lt(comparator_1_lt));
  Comparator #(.mode("unsigned"), .width(32)) comparator_2 (
    .a(rdata1), .b(rdata2), .gt(comparator_2_gt), .eq(comparator_2_eq), .lt(comparator_2_lt));
  or or_1 (or_1_out, comparator_1_gt, comparator_1_eq);
  not not_1 (not_1_out, comparator_1_eq);
  Multiplexer #(.disabled("Z"), .enable("true"), .select(3)) multiplexer_1 (
    .in0(comparator_1_eq), .in1(not_1_out), .in2(1'b0), .in3(1'b0), .in4(comparator_1_lt), .in5(or_1_out),
    .in6(comparator_2_lt), .in7(or_2_out), .out(multiplexer_1_out), .sel(fun3));  // open: en
  or or_2 (or_2_out, comparator_2_eq, comparator_2_gt);
  and and_1 (branch_taken, multiplexer_1_out, branch);
endmodule

module new_alu (
  input  [31:0] rs1,
  input  [31:0] rs2_imm,
  input  [3:0] ALU_Control,
  output [31:0] result,
  output zero
);

  wire comparator_1_lt, comparator_2_lt;
  wire [31:0] adder_1_out, and_1_out, bit_extender_1_out, bit_extender_2_out, or_1_out, shifter_1_out,
       shifter_2_out, shifter_3_out, subtractor_1_out, xor_1_out;

  Adder #(.width(32)) adder_1 (.a(rs1), .b(rs2_imm), .out(adder_1_out));  // open: cin, cout
  Subtractor #(.width(32)) subtractor_1 (.a(rs1), .b(rs2_imm), .out(subtractor_1_out));  // open: bin, bout
  assign and_1_out = rs1 & rs2_imm;  // AND_Gate and_1, 32 bits wide
  assign or_1_out = rs1 | rs2_imm;  // OR_Gate or_1, 32 bits wide
  assign xor_1_out = rs1 ^ rs2_imm;  // XOR_Gate xor_1, 32 bits wide
  Shifter #(.width(32)) shifter_1 (.in(rs1), .\dist (rs2_imm[4:0]), .out(shifter_1_out));
  Shifter #(.shift("lr"), .width(32)) shifter_2 (.in(rs1), .\dist (rs2_imm[4:0]), .out(shifter_2_out));
  Shifter #(.shift("ar"), .width(32)) shifter_3 (.in(rs1), .\dist (rs2_imm[4:0]), .out(shifter_3_out));
  Comparator #(.width(32)) comparator_1 (.a(rs1), .b(rs2_imm), .lt(comparator_1_lt));  // open: gt, eq
  Comparator #(.mode("unsigned"), .width(32)) comparator_2 (
    .a(rs1), .b(rs2_imm), .lt(comparator_2_lt));  // open: gt, eq
  assign bit_extender_1_out = {{31{1'b0}}, comparator_1_lt};  // Bit_Extender bit_extender_1
  assign bit_extender_2_out = {{31{1'b0}}, comparator_2_lt};  // Bit_Extender bit_extender_2
  Multiplexer #(.disabled("Z"), .enable("true"), .select(4), .width(32)) multiplexer_1 (
    .in0(adder_1_out), .in1(subtractor_1_out), .in2(and_1_out), .in3(or_1_out), .in4(xor_1_out),
    .in5(shifter_1_out), .in6(shifter_2_out), .in7(shifter_3_out), .in8(bit_extender_1_out),
    .in9(bit_extender_2_out), .in10(rs2_imm), .in11({32{1'b0}}), .in12({32{1'b0}}), .in13({32{1'b0}}),
    .in14({32{1'b0}}), .in15({32{1'b0}}), .out(result), .sel(ALU_Control));  // open: en
  Comparator #(.width(32)) comparator_3 (.a(result), .b({32{1'b0}}), .eq(zero));  // open: gt, lt

  // Other names for the same wires on the sheet: A[31:0] = rs1; B[31:0] = rs2_imm
endmodule

module processor (
);

  wire alu_src, auipc, branch, branch_taken, clk, comparator_1_eq, jump, lui, mem_read, mem_to_reg,
       mem_write, reg_write, rst, zero;
  wire [1:0] alu_op, pc_sel;
  wire [2:0] fun3;
  wire [3:0] alu_ctrl, multiplexer_3_out, multiplexer_4_out;
  wire [6:0] fun7;
  wire [24:0] instr;
  wire [31:0] adder_2_out, alu_a, alu_b, alu_result, imm, load_out, mem_data, multiplexer_1_out, pc,
       pc_plus_4, rdata1, rdata2, wb_data;

  Adder #(.width(32)) adder_1 (.a(pc), .b(32'h4), .out(pc_plus_4));  // open: cin, cout
  Adder #(.width(32)) adder_2 (.a(pc), .b(imm), .out(adder_2_out));  // open: cin, cout
  Multiplexer #(.disabled("Z"), .enable("true"), .select(2), .width(32)) multiplexer_1 (
    .in0(pc_plus_4), .in1(adder_2_out), .in2(alu_result), .in3({32{1'b0}}), .out(multiplexer_1_out),
    .sel(pc_sel));  // open: en
  Register #(.width(32)) u_PC (.D(multiplexer_1_out), .clk(clk), .Q(pc), .clr(rst));  // open: en
  Button reset (.out(rst));
  Clock clock_1 (.out(clk));
  controlunit controlunit_1 (
    .opcode(instr[6:0]), .reg_write(reg_write), .alu_src(alu_src), .mem_read(mem_read),
    .mem_write(mem_write), .mem_to_reg(mem_to_reg), .branch(branch), .alu_op(alu_op), .jump(jump), .lui(lui),
    .auipc(auipc));
  alucontrol alucontrol_1 (.alu_op(alu_op), .fun3(fun3), .fun7(fun7), .ctrl(alu_ctrl));
  new_alu new_alu_1 (.rs1(alu_a), .rs2_imm(alu_b), .ALU_Control(alu_ctrl), .result(alu_result), .zero(zero));
  Load_Handler load_handler_1 (.mem_data(mem_data), .fun3(fun3), .Load_output(load_out));
  new_regfile new_regfile_1 (
    .Write_data(wb_data), .clk(clk), .rst(rst), .read_data_1(instr[19:15]), .read_data_2(instr[24:20]),
    .EN(reg_write), .Write_Reg(instr[11:7]), .out_data_1(rdata1), .out_data_2(rdata2));
  branchcomparator branchcomparator_1 (
    .rdata1(rdata1), .branch(branch), .rdata2(rdata2), .fun3(fun3), .branch_taken(branch_taken));
  instruction_mem instruction_mem_1 (.in_1(pc), .out_2({fun7, instr[24:15], fun3, instr[11:0]}));
  imm_gen imm_gen_1 (.ins({fun7, instr[24:15], fun3, instr[11:0]}), .imm(imm));
  Multiplexer #(.disabled("Z"), .enable("true"), .select(2), .width(32)) multiplexer_2 (
    .in0(rdata1), .in1({32{1'b0}}), .in2(pc), .in3({32{1'b0}}), .out(alu_a), .sel({auipc, lui}));  // open: en
  Multiplexer #(.disabled("Z"), .enable("true"), .select(3), .width(4)) multiplexer_3 (
    .in0(4'b0001), .in1(4'b0011), .in2(4'b1111), .in3(4'b0000), .in4(4'b0000), .in5(4'b0000), .in6(4'b0000),
    .in7(4'b0000), .out(multiplexer_3_out), .sel(fun3));  // open: en
  Comparator #(.width(7)) comparator_1 (.a(instr[6:0]), .b(7'b1101111), .eq(comparator_1_eq));  // open: gt, lt
  Multiplexer #(.disabled("Z"), .enable("true"), .width(4)) multiplexer_4 (
    .in0(4'b0000), .in1(multiplexer_3_out), .out(multiplexer_4_out), .sel(mem_write));  // open: en
  or or_1 (pc_sel[0], branch_taken, comparator_1_eq);
  Comparator #(.width(7)) comparator_2 (.a(instr[6:0]), .b(7'b1100111), .eq(pc_sel[1]));  // open: gt, lt
  RAM #(.addrWidth(24), .asyncread("true"), .byteenables("byteEnables"), .dataWidth(32)) ram_1 (
    .addr(alu_result[25:2]), .we(mem_write), .oe(1'b1), .clk(clk), .din(rdata2), .dout(mem_data),
    .be3(multiplexer_4_out[3]), .be2(multiplexer_4_out[2]), .be1(multiplexer_4_out[1]),
    .be0(multiplexer_4_out[0]));
  Multiplexer #(.disabled("Z"), .enable("true"), .width(32)) multiplexer_5 (
    .in0(rdata2), .in1(imm), .out(alu_b), .sel(alu_src));  // open: en
  Multiplexer #(.disabled("Z"), .enable("true"), .select(2), .width(32)) multiplexer_6 (
    .in0(alu_result), .in1(load_out), .in2(pc_plus_4), .in3({32{1'b0}}), .out(wb_data),
    .sel({jump, mem_to_reg}));  // open: en

  // Other names for the same wires on the sheet: opcode[6:0] = instr[6:0]; rd[4:0] = instr[11:7];
  //   instr (some bits) = {fun7, fun3}; rs1[4:0] = instr[19:15]; rs2[4:0] = instr[24:20]
endmodule

module controlunit (
  input  [6:0] opcode,
  output reg_write,
  output alu_src,
  output mem_read,
  output mem_write,
  output mem_to_reg,
  output branch,
  output [1:0] alu_op,
  output jump,
  output lui,
  output auipc
);

  wire comparator_1_eq, comparator_2_eq, comparator_6_eq, comparator_7_eq;

  Comparator #(.width(7)) comparator_1 (.a(opcode), .b(7'b0110011), .eq(comparator_1_eq));  // open: gt, lt
  Comparator #(.width(7)) comparator_2 (.a(opcode), .b(7'b0010011), .eq(comparator_2_eq));  // open: gt, lt
  Comparator #(.width(7)) comparator_3 (.a(opcode), .b(7'b0000011), .eq(mem_read));  // open: gt, lt
  Comparator #(.width(7)) comparator_4 (.a(opcode), .b(7'b0100011), .eq(mem_write));  // open: gt, lt
  Comparator #(.width(7)) comparator_5 (.a(opcode), .b(7'b1100011), .eq(branch));  // open: gt, lt
  Comparator #(.width(7)) comparator_6 (.a(opcode), .b(7'b1101111), .eq(comparator_6_eq));  // open: gt, lt
  Comparator #(.width(7)) comparator_7 (.a(opcode), .b(7'b1100111), .eq(comparator_7_eq));  // open: gt, lt
  Comparator #(.width(7)) comparator_8 (.a(opcode), .b(7'b0110111), .eq(lui));  // open: gt, lt
  Comparator #(.width(7)) comparator_9 (.a(opcode), .b(7'b0010111), .eq(auipc));  // open: gt, lt
  or or_1 (reg_write, comparator_1_eq, comparator_2_eq, mem_read, comparator_6_eq, comparator_7_eq, lui, auipc);
  or or_2 (alu_src, comparator_2_eq, mem_read, mem_write, comparator_7_eq, lui, auipc);
  or or_3 (jump, comparator_6_eq, comparator_7_eq);
  or or_4 (alu_op[0], branch, comparator_6_eq, comparator_7_eq, lui, auipc);
  or or_5 (alu_op[1], comparator_1_eq, comparator_2_eq, comparator_6_eq, comparator_7_eq, lui, auipc);

  assign mem_to_reg = mem_read;
endmodule

module alucontrol (
  input  [1:0] alu_op,
  input  [2:0] fun3,
  input  [6:0] fun7,
  output [3:0] ctrl
);

  wire is_alt;
  wire [3:0] multiplexer_1_out, multiplexer_2_out, multiplexer_3_out;

  Multiplexer #(.disabled("Z"), .enable("true"), .width(4)) multiplexer_1 (
    .in0(4'b0110), .in1(4'b0111), .out(multiplexer_1_out), .sel(is_alt));  // open: en
  Multiplexer #(.disabled("Z"), .enable("true"), .width(4)) multiplexer_2 (
    .in0(4'b0000), .in1(4'b0001), .out(multiplexer_2_out), .sel(is_alt));  // open: en
  Multiplexer #(.disabled("Z"), .enable("true"), .select(3), .width(4)) multiplexer_3 (
    .in0(multiplexer_2_out), .in1(4'b0101), .in2(4'b1000), .in3(4'b1001), .in4(4'b0100),
    .in5(multiplexer_1_out), .in6(4'b0011), .in7(4'b0010), .out(multiplexer_3_out), .sel(fun3));  // open: en
  Comparator #(.width(7)) comparator_1 (.a(fun7), .b(7'b0100000), .eq(is_alt));  // open: gt, lt
  Multiplexer #(.disabled("Z"), .enable("true"), .select(2), .width(4)) multiplexer_4 (
    .in0(4'b0000), .in1(4'b0001), .in2(multiplexer_3_out), .in3(4'b0000), .out(ctrl), .sel(alu_op));  // open: en
endmodule

module new_regfile (
  input  [31:0] Write_data,
  input  clk,
  input  rst,
  input  [4:0] read_data_1,
  input  [4:0] read_data_2,
  input  EN,
  input  [4:0] Write_Reg,
  output [31:0] out_data_1,
  output [31:0] out_data_2
);

  wire x0we_t, x1we_t, x2we_t, x3we_t, x4we_t, x5we_t, x6we_t, x7we_t, x8we_t, x9we_t, x10we_t, x11we_t,
       x12we_t, x13we_t, x14we_t, x15we_t, x16we_t, x17we_t, x18we_t, x19we_t, x20we_t, x21we_t, x22we_t,
       x23we_t, x24we_t, x25we_t, x26we_t, x27we_t, x28we_t, x29we_t, x30we_t, x31we_t;
  wire [31:0] x1q_t, x2q_t, x3q_t, x4q_t, x5q_t, x6q_t, x7q_t, x8q_t, x9q_t, x10q_t, x11q_t, x12q_t, x13q_t,
       x14q_t, x15q_t, x16q_t, x17q_t, x18q_t, x19q_t, x20q_t, x21q_t, x22q_t, x23q_t, x24q_t, x25q_t,
       x26q_t, x27q_t, x28q_t, x29q_t, x30q_t, x31q_t;

  Decoder #(.select(5)) decoder_1 (
    .out0(x0we_t), .out1(x1we_t), .out2(x2we_t), .out3(x3we_t), .out4(x4we_t), .out5(x5we_t), .out6(x6we_t),
    .out7(x7we_t), .out8(x8we_t), .out9(x9we_t), .out10(x10we_t), .out11(x11we_t), .out12(x12we_t),
    .out13(x13we_t), .out14(x14we_t), .out15(x15we_t), .out16(x16we_t), .out17(x17we_t), .out18(x18we_t),
    .out19(x19we_t), .out20(x20we_t), .out21(x21we_t), .out22(x22we_t), .out23(x23we_t), .out24(x24we_t),
    .out25(x25we_t), .out26(x26we_t), .out27(x27we_t), .out28(x28we_t), .out29(x29we_t), .out30(x30we_t),
    .out31(x31we_t), .sel(Write_Reg), .en(EN));
  Register #(.width(32)) x4 (.D(Write_data), .en(x4we_t), .clk(clk), .Q(x4q_t), .clr(rst));
  Register #(.width(32)) x8 (.D(Write_data), .en(x8we_t), .clk(clk), .Q(x8q_t), .clr(rst));
  Register #(.width(32)) x12 (.D(Write_data), .en(x12we_t), .clk(clk), .Q(x12q_t), .clr(rst));
  Register #(.width(32)) x16 (.D(Write_data), .en(x16we_t), .clk(clk), .Q(x16q_t), .clr(rst));
  Register #(.width(32)) x20 (.D(Write_data), .en(x20we_t), .clk(clk), .Q(x20q_t), .clr(rst));
  Register #(.width(32)) x24 (.D(Write_data), .en(x24we_t), .clk(clk), .Q(x24q_t), .clr(rst));
  Register #(.width(32)) x28 (.D(Write_data), .en(x28we_t), .clk(clk), .Q(x28q_t), .clr(rst));
  Register #(.width(32)) x1 (.D(Write_data), .en(x1we_t), .clk(clk), .Q(x1q_t), .clr(rst));
  Register #(.width(32)) x5 (.D(Write_data), .en(x5we_t), .clk(clk), .Q(x5q_t), .clr(rst));
  Register #(.width(32)) x9 (.D(Write_data), .en(x9we_t), .clk(clk), .Q(x9q_t), .clr(rst));
  Register #(.width(32)) x13 (.D(Write_data), .en(x13we_t), .clk(clk), .Q(x13q_t), .clr(rst));
  Register #(.width(32)) x17 (.D(Write_data), .en(x17we_t), .clk(clk), .Q(x17q_t), .clr(rst));
  Register #(.width(32)) x21 (.D(Write_data), .en(x21we_t), .clk(clk), .Q(x21q_t), .clr(rst));
  Register #(.width(32)) x25 (.D(Write_data), .en(x25we_t), .clk(clk), .Q(x25q_t), .clr(rst));
  Register #(.width(32)) x29 (.D(Write_data), .en(x29we_t), .clk(clk), .Q(x29q_t), .clr(rst));
  Register #(.width(32)) x2 (.D(Write_data), .en(x2we_t), .clk(clk), .Q(x2q_t), .clr(rst));
  Register #(.width(32)) x6 (.D(Write_data), .en(x6we_t), .clk(clk), .Q(x6q_t), .clr(rst));
  Register #(.width(32)) x10 (.D(Write_data), .en(x10we_t), .clk(clk), .Q(x10q_t), .clr(rst));
  Register #(.width(32)) x14 (.D(Write_data), .en(x14we_t), .clk(clk), .Q(x14q_t), .clr(rst));
  Register #(.width(32)) x18 (.D(Write_data), .en(x18we_t), .clk(clk), .Q(x18q_t), .clr(rst));
  Register #(.width(32)) x22 (.D(Write_data), .en(x22we_t), .clk(clk), .Q(x22q_t), .clr(rst));
  Register #(.width(32)) x26 (.D(Write_data), .en(x26we_t), .clk(clk), .Q(x26q_t), .clr(rst));
  Register #(.width(32)) x30 (.D(Write_data), .en(x30we_t), .clk(clk), .Q(x30q_t), .clr(rst));
  Register #(.width(32)) x3 (.D(Write_data), .en(x3we_t), .clk(clk), .Q(x3q_t), .clr(rst));
  Register #(.width(32)) x7 (.D(Write_data), .en(x7we_t), .clk(clk), .Q(x7q_t), .clr(rst));
  Register #(.width(32)) x11 (.D(Write_data), .en(x11we_t), .clk(clk), .Q(x11q_t), .clr(rst));
  Register #(.width(32)) x15 (.D(Write_data), .en(x15we_t), .clk(clk), .Q(x15q_t), .clr(rst));
  Register #(.width(32)) x19 (.D(Write_data), .en(x19we_t), .clk(clk), .Q(x19q_t), .clr(rst));
  Register #(.width(32)) x23 (.D(Write_data), .en(x23we_t), .clk(clk), .Q(x23q_t), .clr(rst));
  Register #(.width(32)) x27 (.D(Write_data), .en(x27we_t), .clk(clk), .Q(x27q_t), .clr(rst));
  Register #(.width(32)) x31 (.D(Write_data), .en(x31we_t), .clk(clk), .Q(x31q_t), .clr(rst));
  Multiplexer #(.select(5), .width(32)) multiplexer_1 (
    .in0({32{1'b0}}), .in1(x1q_t), .in2(x2q_t), .in3(x3q_t), .in4(x4q_t), .in5(x5q_t), .in6(x6q_t),
    .in7(x7q_t), .in8(x8q_t), .in9(x9q_t), .in10(x10q_t), .in11(x11q_t), .in12(x12q_t), .in13(x13q_t),
    .in14(x14q_t), .in15(x15q_t), .in16(x16q_t), .in17(x17q_t), .in18(x18q_t), .in19(x19q_t), .in20(x20q_t),
    .in21(x21q_t), .in22(x22q_t), .in23(x23q_t), .in24(x24q_t), .in25(x25q_t), .in26(x26q_t), .in27(x27q_t),
    .in28(x28q_t), .in29(x29q_t), .in30(x30q_t), .in31(x31q_t), .out(out_data_1), .sel(read_data_1));
  Multiplexer #(.select(5), .width(32)) multiplexer_2 (
    .in0({32{1'b0}}), .in1(x1q_t), .in2(x2q_t), .in3(x3q_t), .in4(x4q_t), .in5(x5q_t), .in6(x6q_t),
    .in7(x7q_t), .in8(x8q_t), .in9(x9q_t), .in10(x10q_t), .in11(x11q_t), .in12(x12q_t), .in13(x13q_t),
    .in14(x14q_t), .in15(x15q_t), .in16(x16q_t), .in17(x17q_t), .in18(x18q_t), .in19(x19q_t), .in20(x20q_t),
    .in21(x21q_t), .in22(x22q_t), .in23(x23q_t), .in24(x24q_t), .in25(x25q_t), .in26(x26q_t), .in27(x27q_t),
    .in28(x28q_t), .in29(x29q_t), .in30(x30q_t), .in31(x31q_t), .out(out_data_2), .sel(read_data_2));

  // Other names for the same wires on the sheet: clk_t = clk; rd_t[31:0] = Write_data; rst_t = rst
endmodule

module instruction_mem (
  input  [31:0] in_1,
  output [31:0] out_2
);

  ROM #(.addrWidth(24), .dataWidth(32)) rom_1 (.addr(in_1[25:2]), .data(out_2));

  // Notes on the sheet:
  //   contents of rom_1 (hex, n*v repeats v):
  //   c00093 a00113 20f1b3 20e233 20c2b3 209313 13b7 6f
endmodule
